// Logisim project IlyasKarimov_HU.circ as structural Verilog: 1 circuit, main circuit main
module main (
  input  RegWriteM,
  input  [3:0] RA1E,
  input  [3:0] RA2E,
  input  RegWriteW,
  input  [3:0] RA1D,
  input  MemToRegE,
  input  [3:0] RA2D,
  input  [3:0] R1AE,
  input  [3:0] WA3E,
  input  [3:0] WA3M,
  input  [3:0] WA3W,
  input  [3:0] R2AE,
  output [1:0] ForwardAE,
  output [1:0] ForwardBE,
  output LDRInstall
);

  wire comparator_1_eq, comparator_2_eq, comparator_3_eq, comparator_4_eq, comparator_5_eq, comparator_6_eq,
       or_1_out;
  wire [1:0] and_3_out, and_4_out;

  Comparator #(.width(4)) comparator_1 (.a(RA1E), .b(WA3M), .eq(comparator_1_eq));  // open: gt, lt
  Comparator #(.width(4)) comparator_2 (.a(RA2E), .b(WA3M), .eq(comparator_2_eq));  // open: gt, lt
  Comparator #(.width(4)) comparator_3 (.a(RA1E), .b(WA3W), .eq(comparator_3_eq));  // open: gt, lt
  Comparator #(.width(4)) comparator_4 (.a(RA2E), .b(WA3W), .eq(comparator_4_eq));  // open: gt, lt
  Comparator #(.width(4)) comparator_5 (.a(RA1D), .b(WA3E), .eq(comparator_5_eq));  // open: gt, lt
  Comparator #(.width(4)) comparator_6 (.a(RA2D), .b(WA3E), .eq(comparator_6_eq));  // open: gt, lt
  and and_1 (and_3_out[1], RegWriteM, comparator_1_eq);
  and and_2 (and_4_out[1], RegWriteM, comparator_2_eq);
  and and_3 (and_3_out[0], comparator_3_eq, RegWriteW);
  and and_4 (and_4_out[0], RegWriteW, comparator_4_eq);
  or or_1 (or_1_out, comparator_5_eq, comparator_6_eq);
  and and_5 (LDRInstall, MemToRegE, or_1_out);
  Multiplexer #(.select(2), .width(2)) multiplexer_1 (
    .in0(2'b00), .in1(2'b01), .in2(2'b10), .in3(2'b10), .out(ForwardAE), .sel(and_3_out));  // open: en
  Multiplexer #(.select(2), .width(2)) multiplexer_2 (
    .in0(2'b00), .in1(2'b01), .in2(2'b10), .in3(2'b10), .out(ForwardBE), .sel(and_4_out));  // open: en

  // Notes on the sheet:
  //   Match_1E_M
  //   Match_2E_M
  //   Match_1E_W
  //   Match_2E_W
endmodule
