// Logisim project IlyasKarimov_PDI.circ as structural Verilog: 3 circuits, main circuit Splitter
module Splitter (
  input  [31:0] in_1,
  output [3:0] _15_12,
  output [23:0] _23_0,
  output [3:0] _15_12_2,
  output [3:0] _19_16,
  output [3:0] _3_0,
  output [5:0] _25_20,
  output [3:0] _31_28,
  output [1:0] _27_26
);


  assign _3_0 = in_1[3:0];
  assign _15_12 = in_1[15:12];
  assign _15_12_2 = in_1[15:12];
  assign _19_16 = in_1[19:16];
  assign _23_0 = in_1[23:0];
  assign _25_20 = in_1[25:20];
  assign _27_26 = in_1[27:26];
  assign _31_28 = in_1[31:28];
endmodule

module ImmExt (
  input  [23:0] in_1,
  input  [1:0] in_2,
  output [31:0] out_3
);

  wire [31:0] bit_extender_1_out, bit_extender_2_out, bit_extender_3_out, undriven;

  assign bit_extender_1_out = {{24{1'b0}}, in_1[7:0]};  // Bit_Extender bit_extender_1
  assign bit_extender_2_out = {{20{1'b0}}, in_1[11:0]};  // Bit_Extender bit_extender_2
  assign bit_extender_3_out = {{8{in_1[23]}}, in_1};  // Bit_Extender bit_extender_3
  Multiplexer #(.select(2), .width(32)) multiplexer_1 (
    .in0(bit_extender_1_out), .in1(bit_extender_2_out), .in2(bit_extender_3_out), .in3(undriven),
    .out(out_3), .sel(in_2));  // open: en
endmodule

module CondEx (
  input  [1:0] Flags_1_0,
  input  [1:0] Flags_3_2,
  input  [3:0] Cond_3_0,
  output out_4
);

  wire and_1_out, and_2_out, not_1_out, not_2_out, not_3_out, not_4_out, or_1_out, or_2_out, xnor_1_out,
       xor_1_out;

  not not_1 (not_1_out, Flags_3_2[0]);
  not not_2 (not_2_out, Flags_3_2[1]);
  and and_1 (and_1_out, Flags_1_0[1], not_1_out);
  or or_1 (or_1_out, Flags_3_2[0], not_4_out);
  xor xor_1 (xor_1_out, Flags_3_2[1], Flags_1_0[0]);
  not not_3 (not_3_out, Flags_1_0[0]);
  not not_4 (not_4_out, Flags_1_0[1]);
  xnor xnor_1 (xnor_1_out, Flags_3_2[1], Flags_1_0[0]);
  and and_2 (and_2_out, xnor_1_out, not_1_out);
  Multiplexer #(.select(4)) multiplexer_1 (
    .in0(Flags_3_2[0]), .in1(not_1_out), .in2(Flags_1_0[1]), .in3(not_4_out), .in4(Flags_3_2[1]),
    .in5(not_2_out), .in6(Flags_1_0[0]), .in7(not_3_out), .in8(and_1_out), .in9(or_1_out), .in10(xnor_1_out),
    .in11(xor_1_out), .in12(and_2_out), .in13(or_2_out), .in14(1'b1), .in15(1'b1), .out(out_4), .sel(Cond_3_0));  // open: en
  or or_2 (or_2_out, xor_1_out, Flags_3_2[0]);

  // Notes on the sheet:
  //   N
  //   Z
  //   C
  //   V
endmodule
